# Fritzing sketch ClockModule (saved by Fritzing 0.9.3b)
breadboards: 1

parts:
  U1 = attiny85 [package=dip]
  R1 = Rotary Potentiometer (Small) [maximum_resistance=100kΩ package=THT]
  S1 = Pushbutton [package="[THT]"]
  R2 = Resistor [tolerance=±5% resistance=10k package=THT]
  LED1 = LED - 5mm [color="Yellow (595nm)" package="5 mm [THT]"]
  R5 = Resistor [tolerance=±5% resistance=330 package=THT]
  C1 = Electrolytic Capacitor [capacitance=0.1mF voltage=50V package="100 mil [THT, electrolytic]"]
  S2 = Toggle Switch [package=THT]
  R6 = Resistor [tolerance=±5% resistance=10k package=THT]

nets:
  N1: U1.Pin_2, R1.wiper
  N2: U1.Pin_4, R1.leg2, S1.Pin_1, S1.Pin_2, R5.Pin_0, C1.+, S2.L1
  N3: U1.Pin_5, LED1.anode
  N4: U1.Pin_6, S2.COM
  N5: U1.Pin_7, S1.Pin_3, S1.Pin_4, R2.Pin_1
  N6: U1.Pin_8, R1.leg1, R2.Pin_0, C1.-, R6.Pin_1
  N7: LED1.cathode, R5.Pin_1
  N8: S2.L2, R6.Pin_0

// code stored in the sketch: clock_tiny.ino
#define CLK_PIN 0
#define MODE_PIN 1
#define STEP_PIN 2
#define ADJ_PIN 3
#define HALT_PIN 4
long currentMillis = 0;
int AUTOMODE_CURRENT = LOW;
long last_automode_switch = 0;
int adj_value = 0; 

void setup() {
  // set all the pinMode values
  pinMode (CLK_PIN, OUTPUT);
  pinMode (MODE_PIN, INPUT);
  pinMode (STEP_PIN, INPUT);
  pinMode (ADJ_PIN, INPUT);
  pinMode (HALT_PIN, INPUT);
}

void loop() {
  currentMillis = millis();

  //always maintain the auto-clock timing
  autoclock_update();
    
  if (digitalRead(HALT_PIN) == HIGH) {
    //keep the clock pin LOW during HALT
    digitalWrite(CLK_PIN, LOW);
  } else {
    if (digitalRead(MODE_PIN) == LOW) {
      //we're in auto mode
      digitalWrite(CLK_PIN, AUTOMODE_CURRENT);
    }
  }
}

void autoclock_update() {
  adj_value = analogRead(ADJ_PIN);
  long interval = adj_value * 2; 
  if (currentMillis > (last_automode_switch + interval)) {
    last_automode_switch = currentMillis;
    AUTOMODE_CURRENT = AUTOMODE_CURRENT == HIGH ? LOW : HIGH;
  }
}
